// Logisim project ALU.circ as structural Verilog: 2 circuits, main circuit ALU
module ALU (
  input  [31:0] A,
  input  [31:0] B,
  input  [4:0] Shift,
  input  [3:0] Codop,
  input  CarryIn,
  output [31:0] S,
  output [3:0] Flags
);

  wire adder_1_cout, adder_2_cout, and_3_out, and_4_out, and_5_out, and_6_out, and_7_out, and_8_out,
       bitselector_1_out, bitselector_2_out, bitselector_3_out, bitselector_4_out, bitselector_5_out,
       bitselector_6_out, bitselector_7_out, bitselector_8_out, bitselector_9_out, bitselector_10_out,
       bitselector_11_out, bitselector_12_out, bitselector_13_out, CmnR, CmpR, not_1_out, not_4_out,
       not_5_out, resulat_enable_1_enable, subtractor_2_bout, subtractor_3_bout, xor_2_out, xor_3_out,
       xor_4_out, xor_5_out, xor_6_out, xor_7_out, xor_8_out, xor_9_out;
  wire [4:0] C, D;
  wire [31:0] adder_1_out, and_1_out, and_2_out, Cmn, Cmp, multiplexer_1_out, multiplier_1_out,
       negator_2_out, not_2_out, not_3_out, or_1_out, shifter_1_out, shifter_2_out, shifter_3_out,
       shifter_4_out, subtractor_2_out, xor_1_out;

  Negator #(.width(5)) negator_1 (.in(Shift), .out(D));
  Subtractor #(.width(5)) subtractor_1 (.a(Shift), .b(5'b00001), .out(C));  // open: bin, bout
  not not_1 (not_1_out, CarryIn);
  BitSelector #(.width(32)) bitselector_1 (.in(A), .out(bitselector_1_out), .sel({5{1'b1}}));
  assign not_2_out = ~A;  // NOT_Gate not_2, 32 bits wide
  BitSelector #(.width(32)) bitselector_2 (.in(B), .out(bitselector_2_out), .sel({5{1'b1}}));
  BitSelector #(.width(32)) bitselector_3 (.in(Cmn), .out(bitselector_3_out), .sel({5{1'b1}}));
  assign and_1_out = A & B;  // AND_Gate and_1, 32 bits wide
  assign xor_1_out = A ^ B;  // XOR_Gate xor_1, 32 bits wide
  Shifter #(.width(32)) shifter_1 (.in(B), .\dist (Shift), .out(shifter_1_out));
  Shifter #(.shift("lr"), .width(32)) shifter_2 (.in(B), .\dist (Shift), .out(shifter_2_out));
  Shifter #(.shift("ar"), .width(32)) shifter_3 (.in(B), .\dist (Shift), .out(shifter_3_out));
  Adder #(.width(32)) adder_1 (.a(A), .b(B), .out(adder_1_out), .cin(CarryIn), .cout(adder_1_cout));
  Subtractor #(.width(32)) subtractor_2 (
    .a(B), .b(A), .out(subtractor_2_out), .bin(not_1_out), .bout(subtractor_2_bout));
  Shifter #(.shift("rr"), .width(32)) shifter_4 (.in(B), .\dist (Shift), .out(shifter_4_out));
  Negator #(.width(32)) negator_2 (.in(A), .out(negator_2_out));
  Subtractor #(.width(32)) subtractor_3 (.a(B), .b(A), .out(Cmp), .bout(subtractor_3_bout));  // open: bin
  Adder #(.width(32)) adder_2 (.a(A), .b(B), .out(Cmn), .cout(adder_2_cout));  // open: cin
  assign or_1_out = A | B;  // OR_Gate or_1, 32 bits wide
  Multiplier #(.width(32)) multiplier_1 (.a(A), .b(B), .out(multiplier_1_out));  // open: cin, cout
  assign and_2_out = not_2_out & B;  // AND_Gate and_2, 32 bits wide
  assign not_3_out = ~B;  // NOT_Gate not_3, 32 bits wide
  BitSelector #(.width(32)) bitselector_4 (.in(adder_1_out), .out(bitselector_4_out), .sel({5{1'b1}}));
  BitSelector #(.width(32)) bitselector_5 (.in(subtractor_2_out), .out(bitselector_5_out), .sel({5{1'b1}}));
  BitSelector #(.width(32)) bitselector_6 (.in(Cmp), .out(bitselector_6_out), .sel({5{1'b1}}));
  BitSelector #(.width(32)) bitselector_7 (.in(A), .out(bitselector_7_out), .sel({5{1'b1}}));
  BitSelector #(.width(32)) bitselector_8 (.in(B), .out(bitselector_8_out), .sel({5{1'b1}}));
  BitSelector #(.width(32)) bitselector_9 (.in(Cmp), .out(bitselector_9_out), .sel({5{1'b1}}));
  BitSelector #(.width(32)) bitselector_10 (.in(Cmn), .out(bitselector_10_out), .sel({5{1'b1}}));
  not not_4 (not_4_out, subtractor_2_bout);
  and and_3 (and_3_out, bitselector_9_out, ~bitselector_8_out, bitselector_7_out);  // AND_Gate
  and and_4 (and_4_out, ~bitselector_10_out, bitselector_8_out, bitselector_7_out);  // AND_Gate
  and and_5 (and_5_out, ~bitselector_7_out, ~bitselector_8_out, bitselector_10_out);  // AND_Gate
  BitSelector #(.width(32)) bitselector_11 (.in(B), .out(bitselector_11_out), .sel(D));
  BitSelector #(.width(32)) bitselector_12 (.in(B), .out(bitselector_12_out), .sel(C));
  BitSelector #(.width(32)) bitselector_13 (.in(B), .out(bitselector_13_out), .sel(C));
  not not_5 (not_5_out, subtractor_3_bout);
  xor xor_2 (xor_2_out, bitselector_5_out, bitselector_1_out);
  xor xor_3 (xor_3_out, bitselector_5_out, bitselector_2_out);
  xor xor_4 (xor_4_out, bitselector_1_out, bitselector_2_out);
  xor xor_5 (xor_5_out, bitselector_1_out, bitselector_4_out);
  xor xor_6 (xor_6_out, bitselector_1_out, bitselector_6_out);
  xor xor_7 (xor_7_out, bitselector_6_out, bitselector_2_out);
  xor xor_8 (xor_8_out, bitselector_1_out, bitselector_3_out);
  xor xor_9 (xor_9_out, bitselector_1_out, bitselector_2_out);
  and and_6 (and_6_out, ~bitselector_7_out, bitselector_8_out, ~bitselector_9_out);  // AND_Gate
  and and_7 (and_7_out, xor_2_out, xor_3_out);
  and and_8 (and_8_out, xor_4_out, xor_5_out);
  // AND_Gate and_9 has open pins: in0=xor_6_out, in1=xor_7_out, out=open
  // AND_Gate and_10 has open pins: in0=xor_8_out, in1=xor_9_out, out=open
  or or_2 (CmpR, and_3_out, and_6_out);
  or or_3 (CmnR, and_4_out, and_5_out);
  Multiplexer #(.enable("false"), .select(4), .width(32)) multiplexer_1 (
    .in0(and_1_out), .in1(xor_1_out), .in2(shifter_1_out), .in3(shifter_2_out), .in4(shifter_3_out),
    .in5(adder_1_out), .in6(subtractor_2_out), .in7(shifter_4_out), .in8(and_1_out), .in9(negator_2_out),
    .in10(Cmp), .in11(Cmn), .in12(or_1_out), .in13(multiplier_1_out), .in14(and_2_out), .in15(not_3_out),
    .out(multiplexer_1_out), .sel(Codop));
  Multiplexer #(.enable("false"), .select(4)) multiplexer_2 (
    .in0(1'b0), .in1(1'b0), .in2(bitselector_11_out), .in3(bitselector_12_out), .in4(bitselector_13_out),
    .in5(adder_1_cout), .in6(not_4_out), .in7(1'b0), .in8(1'b0), .in9(1'b0), .in10(not_5_out),
    .in11(adder_2_cout), .in12(1'b0), .in13(1'b0), .in14(1'b0), .in15(1'b0), .out(Flags[1]), .sel(Codop));
  Comparator #(.width(32)) comparator_1 (
    .a(multiplexer_1_out), .b({32{1'b0}}), .eq(Flags[2]), .lt(Flags[3]));  // open: gt
  Multiplexer #(.enable("false"), .select(4)) multiplexer_3 (
    .in0(1'b0), .in1(1'b0), .in2(1'b0), .in3(1'b0), .in4(1'b0), .in5(1'b0), .in6(and_7_out), .in7(and_8_out),
    .in8(1'b0), .in9(1'b0), .in10(CmpR), .in11(CmnR), .in12(1'b0), .in13(1'b0), .in14(1'b0), .in15(1'b0),
    .out(Flags[0]), .sel(Codop));
  Multiplexer #(.enable("false"), .width(32)) multiplexer_4 (
    .in0(B), .in1(multiplexer_1_out), .out(S), .sel(resulat_enable_1_enable));
  Resulat_enable resulat_enable_1 (.codop(Codop), .enable(resulat_enable_1_enable));

  // Other names for the same wires on the sheet: A_t[3:0] = Codop; Avalue[31:0] = A; B_t[4:0] = Shift;
  //   Bvalue[31:0] = B

  // Notes on the sheet:
  //   Note: for ROR, C = N
  //   Note 2: assume that shift > 0 for LSL and LSR
endmodule

module Resulat_enable (
  input  [3:0] codop,
  output enable
);

  wire not_1_out, not_2_out;

  not not_1 (not_1_out, codop[3]);
  not not_2 (not_2_out, codop[1]);
  or or_1 (enable, not_1_out, not_2_out, codop[2]);
endmodule
