// Logisim project BancDeRegistres.circ as structural Verilog: 1 circuit, main circuit BancRegistre
// R3
module BancRegistre (
  input  [31:0] DataIn,
  input  Clk,
  input  Reset,
  input  [2:0] RegA,
  input  [2:0] RegDest,
  input  [2:0] RegB,
  output [31:0] R0,
  output [31:0] R1,
  output [31:0] AOut,
  output [31:0] R2,
  output [31:0] R3,
  output [31:0] R4,
  output [31:0] BOut,
  output [31:0] R5,
  output [31:0] R6,
  output [31:0] R7
);

  wire decoder_1_out0, decoder_1_out1, decoder_1_out2, decoder_1_out3, decoder_1_out4, decoder_1_out5,
       decoder_1_out6, decoder_1_out7;
  wire [31:0] R0_t, R1_t, R2_t, R3_t, R4_t, R5_t, R6_t, R7_t;

  Decoder #(.select(3)) decoder_1 (
    .out0(decoder_1_out0), .out1(decoder_1_out1), .out2(decoder_1_out2), .out3(decoder_1_out3),
    .out4(decoder_1_out4), .out5(decoder_1_out5), .out6(decoder_1_out6), .out7(decoder_1_out7), .sel(RegDest));  // open: en
  Register #(.width(32)) register_1 (.D(DataIn), .en(decoder_1_out0), .clk(Clk), .Q(R0), .clr(Reset));
  Register #(.width(32)) register_2 (.D(DataIn), .en(decoder_1_out1), .clk(Clk), .Q(R1), .clr(Reset));
  Register #(.width(32)) register_3 (.D(DataIn), .en(decoder_1_out2), .clk(Clk), .Q(R2), .clr(Reset));
  Register #(.width(32)) register_4 (.D(DataIn), .en(decoder_1_out3), .clk(Clk), .Q(R3), .clr(Reset));
  Register #(.width(32)) register_5 (.D(DataIn), .en(decoder_1_out4), .clk(Clk), .Q(R4), .clr(Reset));
  Register #(.width(32)) register_6 (.D(DataIn), .en(decoder_1_out5), .clk(Clk), .Q(R5), .clr(Reset));
  Register #(.width(32)) register_7 (.D(DataIn), .en(decoder_1_out6), .clk(Clk), .Q(R6), .clr(Reset));
  Register #(.width(32)) register_8 (.D(DataIn), .en(decoder_1_out7), .clk(Clk), .Q(R7), .clr(Reset));
  Multiplexer #(.enable("false"), .select(3), .width(32)) multiplexer_1 (
    .in0(R0_t), .in1(R1_t), .in2(R2_t), .in3(R3_t), .in4(R4_t), .in5(R5_t), .in6(R6_t), .in7(R7_t),
    .out(AOut), .sel(RegA));
  Multiplexer #(.enable("false"), .select(3), .width(32)) multiplexer_2 (
    .in0(R0_t), .in1(R1_t), .in2(R2_t), .in3(R3_t), .in4(R4_t), .in5(R5_t), .in6(R6_t), .in7(R7_t),
    .out(BOut), .sel(RegB));
endmodule
