// Logisim project Ctl_Conditional.circ as structural Verilog: 2 circuits, main circuit Conditional
module Conditional (
  input  [15:0] Instruction,
  input  Enable,
  input  N,
  input  Z,
  input  C,
  input  V,
  output [10:0] Offset,
  output Verified
);

  wire bitselector_2_out, bitselector_5_out, or_1_out, tablecond_1_verified;
  wire [3:0] bitselector_1_out;
  wire [7:0] bitselector_4_out, Imm8;
  wire [10:0] bit_extender_1_out, bitselector_3_out, multiplexer_1_out;

  BitSelector #(.group(4), .width(16)) bitselector_1 (.in(Instruction), .out(bitselector_1_out), .sel(2'b10));
  BitSelector #(.width(16)) bitselector_2 (.in(Instruction), .out(bitselector_2_out), .sel(4'b1100));
  BitSelector #(.group(11), .width(16)) bitselector_3 (.in(Instruction), .out(bitselector_3_out), .sel(1'b0));
  assign bit_extender_1_out = {{3{Imm8[7]}}, Imm8};  // Bit_Extender bit_extender_1
  Multiplexer #(.enable("false"), .width(11)) multiplexer_1 (
    .in0(bitselector_3_out), .in1(bit_extender_1_out), .out(multiplexer_1_out), .sel(bitselector_2_out));
  BitSelector #(.group(8), .width(16)) bitselector_4 (.in(Instruction), .out(bitselector_4_out), .sel(1'b0));
  Multiplexer #(.enable("false"), .width(11)) multiplexer_2 (
    .in0({11{1'b0}}), .in1(multiplexer_1_out), .out(Offset), .sel(Enable));
  TableCond tablecond_1 (.Cond(bitselector_1_out), .N(N), .Z(Z), .C(C), .V(V), .Verified(tablecond_1_verified));
  Multiplexer #(.enable("false"), .width(8)) multiplexer_3 (
    .in0(8'hbd), .in1(bitselector_4_out), .out(Imm8), .sel(tablecond_1_verified));
  BitSelector #(.width(16)) bitselector_5 (.in(Instruction), .out(bitselector_5_out), .sel(4'b1100));
  or or_1 (or_1_out, tablecond_1_verified, ~bitselector_5_out);  // OR_Gate
  and and_1 (Verified, or_1_out, Enable);

  // Other names for the same wires on the sheet: E = Enable; I[15:0] = Instruction
endmodule

module TableCond (
  input  [3:0] Cond,
  input  N,
  input  Z,
  input  C,
  input  V,
  output Verified
);

  wire and_1_out, and_2_out, and_3_out, and_4_out, and_5_out, and_6_out, and_7_out, and_8_out, and_9_out,
       and_10_out, and_11_out, and_12_out, and_13_out, and_14_out, and_15_out, and_16_out, and_17_out,
       and_18_out, and_19_out, and_20_out, not_1_out, not_2_out, not_3_out, not_4_out, not_5_out, not_6_out,
       not_7_out, not_8_out;

  not not_1 (not_1_out, Cond[3]);
  not not_2 (not_2_out, Cond[2]);
  not not_3 (not_3_out, Cond[1]);
  not not_4 (not_4_out, Cond[0]);
  not not_5 (not_5_out, N);
  not not_6 (not_6_out, Z);
  not not_7 (not_7_out, C);
  not not_8 (not_8_out, V);
  and and_1 (and_1_out, not_1_out, not_2_out, not_3_out, not_4_out, Z);
  and and_2 (and_2_out, not_1_out, not_2_out, not_3_out, Cond[0], not_6_out);
  and and_3 (and_3_out, not_2_out, not_3_out, Cond[0], not_6_out, not_7_out);
  and and_4 (and_4_out, not_1_out, not_2_out, Cond[1], not_4_out, C);
  and and_5 (and_5_out, not_1_out, not_2_out, Cond[1], Cond[0], not_7_out);
  and and_6 (and_6_out, not_1_out, Cond[2], not_3_out, not_4_out, N);
  and and_7 (and_7_out, Cond[2], not_4_out, N, not_6_out, V);
  and and_8 (and_8_out, not_1_out, Cond[2], not_3_out, Cond[0], not_5_out);
  and and_9 (and_9_out, Cond[2], not_3_out, Cond[0], not_5_out, V);
  and and_10 (and_10_out, Cond[2], Cond[1], not_4_out, V);
  and and_11 (and_11_out, not_1_out, Cond[2], Cond[1], Cond[0], not_8_out);
  and and_12 (and_12_out, Cond[3], not_2_out, not_3_out, not_4_out, not_6_out, C);
  and and_13 (and_13_out, Cond[3], not_3_out, Cond[0], Z);
  and and_14 (and_14_out, Cond[3], Cond[1], not_4_out, not_5_out, not_8_out);
  and and_15 (and_15_out, Cond[3], Cond[1], not_4_out, N, V);
  and and_16 (and_16_out, Cond[3], not_2_out, Cond[1], Cond[0], not_5_out, V);
  and and_17 (and_17_out, Cond[3], not_2_out, Cond[1], Cond[0], N, not_8_out);
  and and_18 (and_18_out, Cond[3], Cond[2], not_4_out, not_5_out, not_6_out, not_8_out);
  and and_19 (and_19_out, Cond[3], Cond[2], not_3_out, Cond[0], N, not_8_out);
  and and_20 (and_20_out, Cond[3], Cond[2], Cond[1], not_4_out);
  or or_1 (Verified, and_1_out, and_2_out, and_3_out, and_4_out, and_5_out, and_6_out, and_7_out, and_8_out, and_9_out, and_10_out, and_11_out, and_12_out, and_13_out, and_14_out, and_15_out, and_16_out, and_17_out, and_18_out, and_19_out, and_20_out);
endmodule
