// Logisim project Ctl_Flags_APSR.circ as structural Verilog: 1 circuit, main circuit Flags_APSR
module Flags_APSR (
  input  [3:0] Update_Mask,
  input  [3:0] Flags_In,
  input  Clk,
  input  Rst,
  output [3:0] Flags_Out
);

  // AND_Gate and_1 has open pins: in0=Update_Mask[0], in1=Flags_In[0], out=open
  Register register_1 (.clk(Clk), .clr(Rst));  // open: D, en, Q
  // Pins of 1 and 4 bits meet at Flags_In
  // Pins of 1 and 4 bits meet at Update_Mask
endmodule
